// Logisim project MipsF5.circ as structural Verilog: 8 circuits, main circuit main
module main (
  output [3:0] out_1,
  output [3:0] out_2,
  output [3:0] out_3,
  output [3:0] out_4
);

  wire and_1_out, clock_1_out, control_1_alusrc, control_1_branch, control_1_jump, control_1_memread,
       control_1_memtoreg, control_1_memwrite, control_1_regdst, control_1_regwrite, mips_alu_4_bit_1_p4;
  wire [3:0] adder_1_out, control_1_aluop, incrementer_1_p2, multiplexer_1_out, multiplexer_3_out,
       multiplexer_5_out, PC_q, ram_1_data, registers_1_readdata2;
  wire [15:0] rom_1_data;

  Clock clock_1 (.out(clock_1_out));
  Register #(.width(4)) PC (.D(multiplexer_5_out), .en(1'b1), .Q(PC_q), .clk(clock_1_out));  // open: clr
  // Incrementer incrementer_1: pin names not known; wires that end beside it: PC_q, incrementer_1_p2
  ROM #(.addrWidth(4), .dataWidth(16)) rom_1 (.addr(PC_q), .data(rom_1_data));  // open: sel
  Multiplexer #(.width(4)) multiplexer_1 (
    .in0(rom_1_data[7:4]), .in1(rom_1_data[3:0]), .out(multiplexer_1_out), .sel(control_1_regdst), .en(1'b1));
  Control control_1 (
    .OpCode(rom_1_data[15:12]), .Jump(control_1_jump), .Branch(control_1_branch),
    .MemWrite(control_1_memwrite), .MemRead(control_1_memread), .RegWrite(control_1_regwrite),
    .MemToReg(control_1_memtoreg), .ALUsrc(control_1_alusrc), .RegDst(control_1_regdst),
    .ALUop(control_1_aluop));
  Registers registers_1 (
    .ReadRegister1(rom_1_data[11:8]), .ReadRegister2(rom_1_data[7:4]), .WriteRegister(multiplexer_1_out),
    .WriteData(out_1), .RegWrite(control_1_regwrite), .CLK(clock_1_out), .ReadData1(out_4),
    .ReadData2(registers_1_readdata2));
  Multiplexer #(.width(4)) multiplexer_2 (
    .in0(registers_1_readdata2), .in1(rom_1_data[3:0]), .out(out_2), .sel(control_1_alusrc), .en(1'b1));
  // MIPS_ALU_4_bit mips_alu_4_bit_1: pin names not known; wires that end beside it: out_4, out_2, control_1_aluop, mips_alu_4_bit_1_p4, out_3
  Adder #(.width(4)) adder_1 (.a(incrementer_1_p2), .b(rom_1_data[3:0]), .out(adder_1_out));  // open: cin, cout
  and and_1 (and_1_out, control_1_branch, mips_alu_4_bit_1_p4);
  Multiplexer #(.width(4)) multiplexer_3 (
    .in0(incrementer_1_p2), .in1(adder_1_out), .out(multiplexer_3_out), .sel(and_1_out), .en(1'b1));
  RAM #(.addrWidth(4), .dataWidth(4), .bus("separate")) ram_1 (
    .addr(out_3), .din(registers_1_readdata2), .data(ram_1_data), .str(control_1_memwrite),
    .clk(clock_1_out), .ld(control_1_memread), .clr(1'b0));  // open: sel
  Multiplexer #(.width(4)) multiplexer_4 (
    .in0(out_3), .in1(ram_1_data), .out(out_1), .sel(control_1_memtoreg), .en(1'b1));
  Multiplexer #(.width(4)) multiplexer_5 (
    .in0(multiplexer_3_out), .in1(rom_1_data[3:0]), .out(multiplexer_5_out), .sel(control_1_jump), .en(1'b1));

  // Notes on the sheet:
  //   contents of rom_1 (hex, n*v repeats v):
  //   0 c025 9323 a33f 6005 a33f 4731 3741 a44f 8116 a010
endmodule

module Registers (
  input  RegWrite,
  input  [3:0] ReadRegister1,
  input  [3:0] ReadRegister2,
  input  [3:0] WriteRegister,
  input  [3:0] WriteData,
  input  CLK,
  output [3:0] ReadData1,
  output [3:0] ReadData2
);

  wire A0_out, A1_out, A2_out, A3_out, A4_out, A5_out, A6_out, A7_out, decoder_1_out0, decoder_1_out1,
       decoder_1_out2, decoder_1_out3, decoder_1_out4, decoder_1_out5, decoder_1_out6, decoder_1_out7;
  wire [3:0] R0_q, R1_q, R2_q, R3_q, R4_q, R5_q, R6_q, R7_q;

  Decoder #(.select(3)) decoder_1 (
    .out0(decoder_1_out0), .out1(decoder_1_out1), .out2(decoder_1_out2), .out3(decoder_1_out3),
    .out4(decoder_1_out4), .out5(decoder_1_out5), .out6(decoder_1_out6), .out7(decoder_1_out7),
    .sel(WriteRegister[2:0]), .en(1'b1));
  and A0 (A0_out, decoder_1_out0, RegWrite);
  and A1 (A1_out, decoder_1_out1, RegWrite);
  and A2 (A2_out, decoder_1_out2, RegWrite);
  and A3 (A3_out, decoder_1_out3, RegWrite);
  and A4 (A4_out, decoder_1_out4, RegWrite);
  and A5 (A5_out, decoder_1_out5, RegWrite);
  and A6 (A6_out, decoder_1_out6, RegWrite);
  and A7 (A7_out, decoder_1_out7, RegWrite);
  Register #(.width(4)) R0 (.en(A0_out), .Q(R0_q), .clk(CLK), .clr(1'b0));  // open: D
  Register #(.width(4)) R1 (.D(WriteData), .en(A1_out), .Q(R1_q), .clk(CLK), .clr(1'b0));
  Register #(.width(4)) R2 (.D(WriteData), .en(A2_out), .Q(R2_q), .clk(CLK), .clr(1'b0));
  Register #(.width(4)) R3 (.D(WriteData), .en(A3_out), .Q(R3_q), .clk(CLK), .clr(1'b0));
  Register #(.width(4)) R4 (.D(WriteData), .en(A4_out), .Q(R4_q), .clk(CLK), .clr(1'b0));
  Register #(.width(4)) R5 (.D(WriteData), .en(A5_out), .Q(R5_q), .clk(CLK), .clr(1'b0));
  Register #(.width(4)) R6 (.D(WriteData), .en(A6_out), .Q(R6_q), .clk(CLK), .clr(1'b0));
  Register #(.width(4)) R7 (.D(WriteData), .en(A7_out), .Q(R7_q), .clk(CLK), .clr(1'b0));
  Multiplexer #(.select(3), .width(4)) multiplexer_1 (
    .in0(R0_q), .in1(R1_q), .in2(R2_q), .in3(R3_q), .in4(R4_q), .in5(R5_q), .in6(R6_q), .in7(R7_q),
    .out(ReadData1), .sel(ReadRegister1[2:0]), .en(1'b1));
  Multiplexer #(.select(3), .width(4)) multiplexer_2 (
    .in0(R0_q), .in1(R1_q), .in2(R2_q), .in3(R3_q), .in4(R4_q), .in5(R5_q), .in6(R6_q), .in7(R7_q),
    .out(ReadData2), .sel(ReadRegister2[2:0]), .en(1'b1));
endmodule

module Control (
  input  [3:0] OpCode,
  output Jump,
  output Branch,
  output MemWrite,
  output MemRead,
  output RegWrite,
  output MemToReg,
  output ALUsrc,
  output RegDst,
  output [3:0] ALUop
);

  ROM #(.addrWidth(4), .dataWidth(12)) rom_1 (
    .addr(OpCode), .data({ALUop, RegDst, ALUsrc, MemToReg, RegWrite, MemRead, MemWrite, Branch, Jump}));  // open: sel

  // Notes on the sheet:
  //   contents of rom_1 (hex, n*v repeats v):
  //   0 190 150 278 2e4 90 7e3 650 6a2 290 50 690 250
endmodule

// DM
module DataMemory (
  input  MemWrite,
  input  [3:0] Address,
  input  [3:0] WriteData,
  input  CLK,
  input  MemRead,
  output [3:0] ReadData
);

  RAM #(.addrWidth(4), .dataWidth(4), .bus("separate")) ram_1 (
    .addr(Address), .din(WriteData), .data(ReadData), .str(MemWrite), .clk(CLK), .ld(MemRead));  // open: sel, clr
endmodule

// FullCircut
module FullCircuit (
  output [3:0] out_1,
  output [3:0] out_2,
  output [3:0] out_3,
  output [3:0] out_4
);

  wire and_1_out, clock_1_out, control_1_alusrc, control_1_branch, control_1_jump, control_1_memread,
       control_1_memtoreg, control_1_memwrite, control_1_regdst, control_1_regwrite, mips_alu_4_bit_1_p4;
  wire [3:0] adder_1_out, control_1_aluop, datamemory_1_readdata, incrementer_1_p2, multiplexer_1_out,
       multiplexer_4_out, multiplexer_5_out, pc_1_readaddress, registers_1_readdata2;
  wire [15:0] rom_1_data;

  Clock clock_1 (.out(clock_1_out));
  PC pc_1 (.Address(multiplexer_5_out), .CLK(clock_1_out), .ReadAddress(pc_1_readaddress));
  // Incrementer incrementer_1: pin names not known; wires that end beside it: pc_1_readaddress, incrementer_1_p2
  ROM #(.addrWidth(4), .dataWidth(16)) rom_1 (.addr(pc_1_readaddress), .data(rom_1_data));  // open: sel
  Multiplexer #(.width(4)) multiplexer_1 (
    .in0(rom_1_data[7:4]), .in1(rom_1_data[3:0]), .out(multiplexer_1_out), .sel(control_1_regdst), .en(1'b1));
  Control control_1 (
    .OpCode(rom_1_data[15:12]), .Jump(control_1_jump), .Branch(control_1_branch),
    .MemWrite(control_1_memwrite), .MemRead(control_1_memread), .RegWrite(control_1_regwrite),
    .MemToReg(control_1_memtoreg), .ALUsrc(control_1_alusrc), .RegDst(control_1_regdst),
    .ALUop(control_1_aluop));
  Registers registers_1 (
    .ReadRegister1(rom_1_data[11:8]), .ReadRegister2(rom_1_data[7:4]), .WriteRegister(multiplexer_1_out),
    .WriteData(out_1), .RegWrite(control_1_regwrite), .CLK(clock_1_out), .ReadData1(out_4),
    .ReadData2(registers_1_readdata2));
  Multiplexer #(.width(4)) multiplexer_2 (
    .in0(registers_1_readdata2), .in1(rom_1_data[3:0]), .out(out_2), .sel(control_1_alusrc), .en(1'b1));
  // MIPS_ALU_4_bit mips_alu_4_bit_1: pin names not known; wires that end beside it: out_4, out_2, control_1_aluop, mips_alu_4_bit_1_p4, out_3
  Adder #(.width(4)) adder_1 (.a(incrementer_1_p2), .b(rom_1_data[3:0]), .out(adder_1_out));  // open: cin, cout
  DataMemory datamemory_1 (
    .Address(out_3), .WriteData(registers_1_readdata2), .MemWrite(control_1_memwrite),
    .MemRead(control_1_memread), .CLK(clock_1_out), .ReadData(datamemory_1_readdata));
  and and_1 (and_1_out, control_1_branch, mips_alu_4_bit_1_p4);
  Multiplexer #(.width(4)) multiplexer_3 (
    .in0(out_3), .in1(datamemory_1_readdata), .out(out_1), .sel(control_1_memtoreg), .en(1'b1));
  Multiplexer #(.width(4)) multiplexer_4 (
    .in0(incrementer_1_p2), .in1(adder_1_out), .out(multiplexer_4_out), .sel(and_1_out), .en(1'b1));
  Multiplexer #(.width(4)) multiplexer_5 (
    .in0(multiplexer_4_out), .in1(rom_1_data[3:0]), .out(multiplexer_5_out), .sel(control_1_jump), .en(1'b1));

  // Notes on the sheet:
  //   contents of rom_1 (hex, n*v repeats v):
  //   0 c025 9323 a33f 6665 a33f 4031 3041 a44f
endmodule

// IM
module InstructionMemory (
  input  [3:0] ReadAddress,
  output [15:0] Instruction
);

  ROM #(.addrWidth(4), .dataWidth(16)) rom_1 (.addr(ReadAddress), .data(Instruction));  // open: sel

  // Notes on the sheet:
  //   contents of rom_1 (hex, n*v repeats v):
  //   2233 c245 8332 c334 533f a33e 6755 822a
endmodule

module PC (
  input  [3:0] Address,
  input  CLK,
  output [3:0] ReadAddress
);

  Register #(.width(4)) PC (.D(Address), .en(1'b1), .Q(ReadAddress), .clk(CLK));  // open: clr
endmodule

module Final (
  output [3:0] out_1,
  output [3:0] out_2,
  output [3:0] out_3,
  output [3:0] out_4
);

  wire and_1_out, clock_1_out, control_1_alusrc, control_1_branch, control_1_jump, control_1_memread,
       control_1_memtoreg, control_1_memwrite, control_1_regdst, control_1_regwrite, mips_alu_4_bit_1_p4;
  wire [3:0] adder_1_out, control_1_aluop, incrementer_1_p2, multiplexer_1_out, multiplexer_3_out,
       multiplexer_5_out, PC_q, ram_1_data, registers_1_readdata2;
  wire [15:0] rom_1_data;

  Clock clock_1 (.out(clock_1_out));
  Register #(.width(4)) PC (.D(multiplexer_5_out), .en(1'b1), .Q(PC_q), .clk(clock_1_out));  // open: clr
  // Incrementer incrementer_1: pin names not known; wires that end beside it: PC_q, incrementer_1_p2
  ROM #(.addrWidth(4), .dataWidth(16)) rom_1 (.addr(PC_q), .data(rom_1_data));  // open: sel
  Multiplexer #(.width(4)) multiplexer_1 (
    .in0(rom_1_data[7:4]), .in1(rom_1_data[3:0]), .out(multiplexer_1_out), .sel(control_1_regdst), .en(1'b1));
  Control control_1 (
    .OpCode(rom_1_data[15:12]), .Jump(control_1_jump), .Branch(control_1_branch),
    .MemWrite(control_1_memwrite), .MemRead(control_1_memread), .RegWrite(control_1_regwrite),
    .MemToReg(control_1_memtoreg), .ALUsrc(control_1_alusrc), .RegDst(control_1_regdst),
    .ALUop(control_1_aluop));
  Registers registers_1 (
    .ReadRegister1(rom_1_data[11:8]), .ReadRegister2(rom_1_data[7:4]), .WriteRegister(multiplexer_1_out),
    .WriteData(out_1), .RegWrite(control_1_regwrite), .CLK(clock_1_out), .ReadData1(out_4),
    .ReadData2(registers_1_readdata2));
  Multiplexer #(.width(4)) multiplexer_2 (
    .in0(registers_1_readdata2), .in1(rom_1_data[3:0]), .out(out_2), .sel(control_1_alusrc), .en(1'b1));
  // MIPS_ALU_4_bit mips_alu_4_bit_1: pin names not known; wires that end beside it: out_4, out_2, control_1_aluop, mips_alu_4_bit_1_p4, out_3
  Adder #(.width(4)) adder_1 (.a(incrementer_1_p2), .b(rom_1_data[3:0]), .out(adder_1_out));  // open: cin, cout
  and and_1 (and_1_out, control_1_branch, mips_alu_4_bit_1_p4);
  Multiplexer #(.width(4)) multiplexer_3 (
    .in0(incrementer_1_p2), .in1(adder_1_out), .out(multiplexer_3_out), .sel(and_1_out), .en(1'b1));
  RAM #(.addrWidth(4), .dataWidth(4), .bus("separate")) ram_1 (
    .addr(out_3), .din(registers_1_readdata2), .data(ram_1_data), .str(control_1_memwrite),
    .clk(clock_1_out), .ld(control_1_memread), .clr(1'b0));  // open: sel
  Multiplexer #(.width(4)) multiplexer_4 (
    .in0(out_3), .in1(ram_1_data), .out(out_1), .sel(control_1_memtoreg), .en(1'b1));
  Multiplexer #(.width(4)) multiplexer_5 (
    .in0(multiplexer_3_out), .in1(rom_1_data[3:0]), .out(multiplexer_5_out), .sel(control_1_jump), .en(1'b1));

  // Notes on the sheet:
  //   contents of rom_1 (hex, n*v repeats v):
  //   0 c025 9323 a33f 6665 a33f 4031 3041 a44f 8116
endmodule
